# Fritzing sketch circuit (saved by Fritzing 0.9.3b)

parts:
  hc-sr1 = hc-sr04
  Raspberry_Pi_1 = Raspberry Pi 3 [part_number=RPI-3-V1.2]
  J1 = Piezo Speaker  # not connected

nets:
  VCC: hc-sr1.VCC, Raspberry_Pi_1.3v3
  N1: hc-sr1.Trig, Raspberry_Pi_1.GIPO17
  N2: hc-sr1.Echo, Raspberry_Pi_1.GIPO27
  GND: hc-sr1.GND, Raspberry_Pi_1.GND
